// Logisim project MIPS.circ as structural Verilog: 5 circuits, main circuit main
module main (
  input  PC_clear,
  input  mem_clr,
  input  reg_clr
);

  wire and_1_out, CLK_out, control_unit_1_alu_src, control_unit_1_b_inv, control_unit_1_bruch,
       control_unit_1_cin, control_unit_1_jmp, control_unit_1_ld, control_unit_1_mem_en,
       control_unit_1_mem_to_reg, control_unit_1_reg_dest, control_unit_1_str, control_unit_1_wc,
       n1_bit_alu_1_zero;
  wire [1:0] control_unit_1_out_2;
  wire [2:0] multiplexer_1_out;
  wire [4:0] rom_1_data_2;
  wire [8:0] rom_1_data;
  wire [13:0] adder_1_out, bit_extender_1_out, bit_extender_2_out, multiplexer_2_out, multiplexer_3_out,
       multiplexer_4_out, multiplexer_5_out, n1_bit_alu_1_f, n8bit_register_file_1_read_data_1,
       n8bit_register_file_1_read_data_2, ram_1_data, register_1_q;

  Register #(.width(14)) register_1 (
    .D(multiplexer_4_out), .Q(register_1_q), .clk(CLK_out), .clr(PC_clear));  // open: en
  Button CLK (.out(CLK_out));
  Adder #(.width(14)) adder_1 (.a(14'h1), .b(register_1_q), .out(adder_1_out));  // open: cin, cout
  ROM #(.addrWidth(14), .dataWidth(14)) rom_1 (.addr(register_1_q), .data({rom_1_data_2, rom_1_data}));  // open: sel
  control_unit control_unit_1 (
    .in_1(rom_1_data_2), .out_2(control_unit_1_out_2), .b_inv(control_unit_1_b_inv),
    .cin(control_unit_1_cin), .wc(control_unit_1_wc), .alu_src(control_unit_1_alu_src),
    .str(control_unit_1_str), .mem_en(control_unit_1_mem_en), .bruch(control_unit_1_bruch),
    .reg_dest(control_unit_1_reg_dest), .mem_to_reg(control_unit_1_mem_to_reg), .Ld(control_unit_1_ld),
    .jmp(control_unit_1_jmp));
  Multiplexer #(.width(3)) multiplexer_1 (
    .in0(rom_1_data[2:0]), .in1(rom_1_data[5:3]), .out(multiplexer_1_out), .sel(control_unit_1_reg_dest));  // open: en
  assign bit_extender_1_out = {{11{1'b0}}, rom_1_data[2:0]};  // Bit_Extender bit_extender_1
  _8bit_register_file u_8bit_register_file_1 (
    .rs(rom_1_data[8:6]), .Write_register(multiplexer_1_out), .rt(rom_1_data[5:3]), .clear(reg_clr),
    .wc(control_unit_1_wc), .clk(CLK_out), .Write_data(multiplexer_5_out),
    .read_data_1(n8bit_register_file_1_read_data_1), .read_data_2(n8bit_register_file_1_read_data_2));
  assign bit_extender_2_out = {{5{1'b0}}, rom_1_data};  // Bit_Extender bit_extender_2
  Multiplexer #(.width(14)) multiplexer_2 (
    .in0(n8bit_register_file_1_read_data_2), .in1(bit_extender_1_out), .out(multiplexer_2_out),
    .sel(control_unit_1_alu_src));  // open: en
  _1_bit_ALU u_1_bit_alu_1 (
    .A(n8bit_register_file_1_read_data_1), .B(multiplexer_2_out), .F(n1_bit_alu_1_f),
    .ALUOP(control_unit_1_out_2), .Cin(control_unit_1_cin), .Binv(control_unit_1_b_inv),
    .zero(n1_bit_alu_1_zero));  // open: Cout
  Multiplexer #(.width(14)) multiplexer_3 (
    .in0(adder_1_out), .in1(bit_extender_1_out), .out(multiplexer_3_out), .sel(and_1_out));  // open: en
  and and_1 (and_1_out, n1_bit_alu_1_zero, control_unit_1_bruch);
  Multiplexer #(.width(14)) multiplexer_4 (
    .in0(multiplexer_3_out), .in1(bit_extender_2_out), .out(multiplexer_4_out), .sel(control_unit_1_jmp));  // open: en
  RAM #(.addrWidth(14), .dataWidth(14), .bus("separate")) ram_1 (
    .addr(n1_bit_alu_1_f), .din(n8bit_register_file_1_read_data_2), .data(ram_1_data),
    .str(control_unit_1_str), .sel(control_unit_1_mem_en), .clk(CLK_out), .ld(control_unit_1_ld),
    .clr(mem_clr));
  Multiplexer #(.width(14)) multiplexer_5 (
    .in0(n1_bit_alu_1_f), .in1(ram_1_data), .out(multiplexer_5_out), .sel(control_unit_1_mem_to_reg));  // open: en
endmodule

module _1_bit_ALU (
  input  [13:0] A,
  input  [13:0] B,
  input  [1:0] ALUOP,
  input  Cin,
  input  Binv,
  output [13:0] F,
  output zero,
  output Cout
);

  wire comparator_1_lt;
  wire [3:0] bit_extender_1_out;
  wire [13:0] adder_1_out, and_1_out, bit_extender_2_out, multiplexer_1_out, not_1_out, shifter_1_out;

  Bit_Extender #(.in_width(14), .out_width(4)) bit_extender_1 (.in(B), .out(bit_extender_1_out));
  assign and_1_out = A & B;  // AND_Gate and_1, 14 bits wide
  Comparator #(.width(14)) comparator_1 (.a(A), .b(B), .eq(zero), .lt(comparator_1_lt));  // open: gt
  Multiplexer #(.width(14), .enable("false")) multiplexer_1 (
    .in0(B), .in1(not_1_out), .out(multiplexer_1_out), .sel(Binv));
  assign not_1_out = ~B;  // NOT_Gate not_1, 14 bits wide
  Shifter #(.width(14)) shifter_1 (.in(A), .\dist (bit_extender_1_out), .out(shifter_1_out));
  assign bit_extender_2_out = {{13{1'b0}}, comparator_1_lt};  // Bit_Extender bit_extender_2
  Adder #(.width(14)) adder_1 (.a(A), .b(multiplexer_1_out), .out(adder_1_out), .cin(Cin), .cout(Cout));
  Multiplexer #(.select(2), .width(14), .enable("false")) multiplexer_2 (
    .in0(shifter_1_out), .in1(and_1_out), .in2(bit_extender_2_out), .in3(adder_1_out), .out(F), .sel(ALUOP));
endmodule

module _8bit_register_file (
  input  [2:0] rs,
  input  [2:0] Write_register,
  input  [2:0] rt,
  input  clear,
  input  wc,
  input  clk,
  input  [13:0] Write_data,
  output [13:0] read_data_1,
  output [13:0] read_data_2
);

  wire and_1_out, and_2_out, and_3_out, and_4_out, and_5_out, and_6_out, and_7_out, and_8_out,
       decoder_1_out0, decoder_1_out1, decoder_1_out2, decoder_1_out3, decoder_1_out4, decoder_1_out5,
       decoder_1_out6, decoder_1_out7;
  wire [13:0] register_1_q, register_2_q, register_3_q, register_4_q, register_5_q, register_6_q,
       register_7_q, register_8_q;

  Decoder #(.select(3)) decoder_1 (
    .out0(decoder_1_out0), .out1(decoder_1_out1), .out2(decoder_1_out2), .out3(decoder_1_out3),
    .out4(decoder_1_out4), .out5(decoder_1_out5), .out6(decoder_1_out6), .out7(decoder_1_out7),
    .sel(Write_register));  // open: en
  and and_1 (and_1_out, decoder_1_out0, wc);
  and and_2 (and_2_out, decoder_1_out1, wc);
  and and_3 (and_3_out, decoder_1_out2, wc);
  and and_4 (and_4_out, decoder_1_out3, wc);
  and and_5 (and_5_out, decoder_1_out4, wc);
  and and_6 (and_6_out, decoder_1_out5, wc);
  and and_7 (and_7_out, decoder_1_out6, wc);
  and and_8 (and_8_out, decoder_1_out7, wc);
  Register #(.width(14)) register_1 (.D(Write_data), .en(and_1_out), .Q(register_1_q), .clk(clk), .clr(clear));
  Register #(.width(14)) register_2 (.D(Write_data), .en(and_2_out), .Q(register_2_q), .clk(clk), .clr(clear));
  Register #(.width(14)) register_3 (.D(Write_data), .en(and_3_out), .Q(register_3_q), .clk(clk), .clr(clear));
  Register #(.width(14)) register_4 (.D(Write_data), .en(and_4_out), .Q(register_4_q), .clk(clk), .clr(clear));
  Register #(.width(14)) register_5 (.D(Write_data), .en(and_5_out), .Q(register_5_q), .clk(clk), .clr(clear));
  Register #(.width(14)) register_6 (.D(Write_data), .en(and_6_out), .Q(register_6_q), .clk(clk), .clr(clear));
  Register #(.width(14)) register_7 (.D(Write_data), .en(and_7_out), .Q(register_7_q), .clk(clk), .clr(clear));
  Register #(.width(14)) register_8 (.D(Write_data), .en(and_8_out), .Q(register_8_q), .clk(clk), .clr(clear));
  Multiplexer #(.select(3), .width(14)) multiplexer_1 (
    .in0(register_1_q), .in1(register_2_q), .in2(register_3_q), .in3(register_4_q), .in4(register_5_q),
    .in5(register_6_q), .in6(register_7_q), .in7(register_8_q), .out(read_data_1), .sel(rs));  // open: en
  Multiplexer #(.select(3), .width(14)) multiplexer_2 (
    .in0(register_1_q), .in1(register_2_q), .in2(register_3_q), .in3(register_4_q), .in4(register_5_q),
    .in5(register_6_q), .in6(register_7_q), .in7(register_8_q), .out(read_data_2), .sel(rt));  // open: en
endmodule

module control_unit (
  input  [4:0] in_1,
  output [1:0] out_2,
  output b_inv,
  output cin,
  output wc,
  output alu_src,
  output str,
  output mem_en,
  output bruch,
  output reg_dest,
  output mem_to_reg,
  output Ld,
  output jmp
);

  wire decoder_1_out0, decoder_1_out1, decoder_1_out5, decoder_1_out6, decoder_1_out7, decoder_1_out8;

  Decoder #(.select(5)) decoder_1 (
    .out0(decoder_1_out0), .out1(decoder_1_out1), .out2(b_inv), .out3(str), .out4(bruch),
    .out5(decoder_1_out5), .out6(decoder_1_out6), .out7(decoder_1_out7), .out8(decoder_1_out8), .out9(Ld),
    .out10(jmp), .sel(in_1));  // open: out11, out12, out13, out14, out15, out16, out17, out18, out19, out20, out21, out22, out23, out24, out25, out26, out27, out28, out29, out30, out31, en
  or or_1 (out_2[0], decoder_1_out0, b_inv, str, decoder_1_out6, decoder_1_out8, Ld);
  or or_2 (out_2[1], decoder_1_out0, b_inv, str, decoder_1_out7, decoder_1_out8, Ld);
  or or_3 (wc, decoder_1_out0, decoder_1_out1, b_inv, decoder_1_out6, decoder_1_out7, decoder_1_out8, Ld);
  or or_4 (alu_src, str, Ld, decoder_1_out8);
  or or_5 (mem_en, str, Ld);
  or or_6 (reg_dest, decoder_1_out8, Ld);

  assign cin = b_inv;
  assign mem_to_reg = Ld;
endmodule

module _8_bit_alu (
  input  [13:0] A,
  input  [13:0] B,
  input  [1:0] ALUOP,
  input  Cin,
  input  Binv,
  output [13:0] F,
  output zero,
  output Cout
);

  wire comparator_1_lt;
  wire [3:0] bit_extender_1_out;
  wire [13:0] adder_1_out, and_1_out, bit_extender_2_out, multiplexer_1_out, not_1_out, shifter_1_out;

  Bit_Extender #(.in_width(14), .out_width(4)) bit_extender_1 (.in(B), .out(bit_extender_1_out));
  assign and_1_out = A & B;  // AND_Gate and_1, 14 bits wide
  Comparator #(.width(14)) comparator_1 (.a(A), .b(B), .eq(zero), .lt(comparator_1_lt));  // open: gt
  Multiplexer #(.width(14), .enable("false")) multiplexer_1 (
    .in0(B), .in1(not_1_out), .out(multiplexer_1_out), .sel(Binv));
  assign not_1_out = ~B;  // NOT_Gate not_1, 14 bits wide
  Shifter #(.width(14)) shifter_1 (.in(A), .\dist (bit_extender_1_out), .out(shifter_1_out));
  assign bit_extender_2_out = {{13{1'b0}}, comparator_1_lt};  // Bit_Extender bit_extender_2
  Adder #(.width(14)) adder_1 (.a(A), .b(multiplexer_1_out), .out(adder_1_out), .cin(Cin), .cout(Cout));
  Multiplexer #(.select(2), .width(14), .enable("false")) multiplexer_2 (
    .in0(shifter_1_out), .in1(and_1_out), .in2(bit_extender_2_out), .in3(adder_1_out), .out(F), .sel(ALUOP));
endmodule
